# Fritzing sketch wiringBRAND (saved by Fritzing 0.9.7b)

parts:
  Part1 = Arduino Mega 2560 (Rev3)
  M3 = fc-51 [package=THT]
  M2 = fc-51 [package=THT]
  M1 = fc-51 [package=THT]
  M4 = fc-51 [package=THT]
  M5 = fc-51 [package=THT]
  M6 = fc-51 [package=THT]
  M7 = fc-51 [package=THT]
  M8 = fc-51 [package=THT]
  M9 = fc-51 [package=THT]
  M10 = fc-51 [package=THT]
  HC-SR04_Sensor_1 = HC-SR04 Ultrasonic Distance Sensor
  HC-SR04_Sensor_2 = HC-SR04 Ultrasonic Distance Sensor
  MD03A1 = Dual VNH2SP30 Motor Driver [part_number=MD03A]
  U1 = LIPO-2000mAh [package=lipo-2000]
  M11 = RioRand LM2596
  M12 = RioRand LM2596
  M13 = RioRand LM2596
  M15 = gear-motor
  M16 = gear-motor
  CUI-enc1 = AMT103
  CUI-enc2 = AMT103
  J1 = Infrared Proximity Sensor

nets:
  N1: Part1.A8, M8.pin1
  N2: Part1.A9, M10.pin1
  N3: Part1.A10, J1.Vout
  N4: Part1.A0, M9.pin1
  N5: Part1.A1, M1.pin1
  N6: Part1.A2, M2.pin1
  N7: Part1.A3, M3.pin1
  N8: Part1.A4, M4.pin1
  N9: Part1.A5, M6.pin1
  N10: Part1.A6, M7.pin1
  N11: Part1.A7, M5.pin1
  N12: Part1.D2_PWM, MD03A1.2PWM
  N13: Part1.D3_PWM, MD03A1.PWM
  N14: Part1.D22, MD03A1.2INb#142
  N15: Part1.D23, MD03A1.2INb#143
  N16: Part1.D26, MD03A1.1INa
  N17: Part1.D27, MD03A1.1INb
  N18: Part1.D38, CUI-enc2.B
  N19: Part1.D39, CUI-enc2.A
  N20: Part1.D42, CUI-enc1.B
  N21: Part1.D43, CUI-enc1.A
  N22: Part1.D46, HC-SR04_Sensor_2.TRIG
  N23: Part1.D47, HC-SR04_Sensor_2.ECHO
  N24: Part1.D52, HC-SR04_Sensor_1.TRIG
  N25: Part1.D53, HC-SR04_Sensor_1.ECHO
  N26: MD03A1.OUT_1A, M16.pin_1
  N27: MD03A1.OUT_1B, M16.pin_2
  N28: MD03A1.OUT_2A, M15.pin_1
  N29: MD03A1.OUT_2B, M15.pin_2
  N30: MD03A1.VIN, M11.Pin_3
  N31: MD03A1.GND, M11.Pin_4
  N32: U1.+, M11.Pin_1, M12.Pin_1, M13.Pin_1
  N33: U1.-, M11.Pin_2, M12.Pin_2, M13.Pin_2

notes:
  9V-Motors
  5V-VCC
  7V-ArduinoMEGA
  GND
  7V-VCC
